# Fritzing sketch onlab_arduino (saved by Fritzing 0.9.3b)
breadboards: 1

parts:
  Part1 = Arduino Uno (Rev3)
  DHT1 = DHT11 Humitidy and Temperature Sensor
  R1 = Resistor [tolerance=±5% resistance=10k package=THT]
  Part2 = Bluetooth HC-05 Macho
  R2 = Resistor [tolerance=±5% resistance=2k package=THT]
  R3 = Resistor [tolerance=±5% resistance=1k package=THT]
  Part3 = BH1750
  Part4 = Adafruit BMP180

nets:
  N1: Part1.A0, Part3.SCL
  N2: Part1.A1, Part3.SDA
  N3: Part1.A2, Part4.SDA
  N4: Part1.A3, Part4.SCL
  N5: Part1.D0/RX, Part2.TXD
  N6: Part1.D1/TX, R3.Pin_0
  N7: Part1.D2, DHT1.DATA, R1.Pin_0
  N8: Part1.ioref, Part3.VCC
  5V: Part1.5V, DHT1.VDD, R1.Pin_1, Part2.VCC
  GND: Part1.GND, DHT1.GND, Part2.GND, R2.Pin_1
  N9: Part2.RXD, R2.Pin_0, R3.Pin_1

custom parts:
  DHT11 Humitidy and Temperature Sensor: DHT11 Humidity and Temperature Sensor
  BH1750: Light Sensor
  Adafruit BMP180: This precision sensor from Bosch is the best low-cost sensing solution for measuring barometric pressure and temperature. Because pressure changes with altitude you can also use it as an altimeter! The sensor is soldered onto a PCB with a 3.3V regulator, I2C level shifter and pull-up resistors on the I2C pins. The BMP180 is the next-generation of sensors from Bosch, and replaces the BMP085.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
